// Logisim project Lab01_Mux21.circ as structural Verilog: 1 circuit, main circuit main
module main (
  input  S,
  input  A,
  input  B,
  output out_4
);

  wire and_1_out, and_2_out, not_1_out, not_2_out;

  not not_1 (not_1_out, S);
  not not_2 (not_2_out, not_1_out);
  and and_1 (and_1_out, not_2_out, A);
  and and_2 (and_2_out, not_1_out, B);
  or or_1 (out_4, and_1_out, and_2_out);

  // Notes on the sheet:
  //   Имя: Жасулан Лабораторная работа: 01  Название схемы: Simple Multiplexer  
endmodule
