// Logisim project Lab02_Bool.circ as structural Verilog: 3 circuits, main circuit main
module main (
  input  A1,
  input  B1,
  input  C1,
  input  A2,
  input  B2,
  input  C2,
  input  D2,
  output True1,
  output True2
);

  Equation_1 equation_1_1 (.A(A1), .B(B1), .C(C1), .out_4(True1));
  Equation_2 equation_2_1 (.A(A2), .B(B2), .C(C2), .D(D2), .OUT(True2));

  // Notes on the sheet:
  //   Name: Zhassulan Lab: Lab 02 Date: 15.02.25
endmodule

module Equation_1 (
  input  A,
  input  B,
  input  C,
  output out_4
);

  wire and_1_out, and_2_out, and_3_out;

  and and_1 (and_1_out, ~A, B, ~C);  // AND_Gate
  and and_2 (and_2_out, A, ~B, ~C);  // AND_Gate
  and and_3 (and_3_out, A, B, C);
  or or_1 (out_4, and_1_out, and_2_out, and_3_out);

  // Notes on the sheet:
  //   OUT
endmodule

module Equation_2 (
  input  A,
  input  B,
  input  C,
  input  D,
  output OUT
);

  wire and_1_out, and_2_out, and_3_out, and_4_out;

  and and_1 (and_1_out, ~A, ~B, C, ~D);  // AND_Gate
  and and_2 (and_2_out, ~A, B, C, D);  // AND_Gate
  and and_3 (and_3_out, A, ~B, C, ~D);  // AND_Gate
  and and_4 (and_4_out, A, B, C, ~D);  // AND_Gate
  or or_1 (OUT, and_1_out, and_2_out, and_3_out, and_4_out);

  // Notes on the sheet:
  //   (A ′  B ′  CD ′  )+(A ′  BCD)+(AB ′  CD ′  )+(ABCD ′  )
endmodule
