// Logisim project 1bit_adder.circ as structural Verilog: 1 circuit, main circuit main
module main (
  input  A,
  input  B,
  output out_3,
  output cout
);

  wire and_1_out, and_2_out;

  and and_1 (and_1_out, ~A, B);  // AND_Gate
  and and_2 (and_2_out, A, ~B);  // AND_Gate
  and and_3 (cout, A, B);
  or or_1 (out_3, and_1_out, and_2_out);

  // Notes on the sheet:
  //   S=(A ′B)+(AB ′)
endmodule
