// Logisim project lab_05.circ as structural Verilog: 8 circuits, main circuit main
module main (
  input  in_1,
  input  in_2,
  input  [2:0] in_3
);

  wire [3:0] universal_1_out_4;

  // Probe on universal_1_out_4
  Universal universal_1 (.clk(in_1), .rst(in_2), .in_3(in_3), .out_4(universal_1_out_4));
  Hex_Digit_Display hex_digit_display_1 (.value(universal_1_out_4));  // open: dp
endmodule

module Asynchronous_Up_Counter (
  input  clk,
  input  rst,
  output [3:0] Up
);

  wire d_ff_1_qn, d_ff_2_qn, d_ff_3_qn, d_ff_4_qn;

  D_Flip_Flop d_ff_1 (.D(d_ff_1_qn), .clk(clk), .Q(Up[0]), .Qn(d_ff_1_qn), .reset(rst));  // open: preset
  D_Flip_Flop d_ff_2 (.D(d_ff_2_qn), .clk(d_ff_1_qn), .Q(Up[1]), .Qn(d_ff_2_qn), .reset(rst));  // open: preset
  D_Flip_Flop d_ff_3 (.D(d_ff_3_qn), .clk(d_ff_2_qn), .Q(Up[2]), .Qn(d_ff_3_qn), .reset(rst));  // open: preset
  D_Flip_Flop d_ff_4 (.D(d_ff_4_qn), .clk(d_ff_3_qn), .Q(Up[3]), .Qn(d_ff_4_qn), .reset(rst));  // open: preset
endmodule

module Asynchronous_Down_Counter (
  input  clk,
  input  rst,
  output [3:0] Up
);

  wire d_ff_1_qn, d_ff_2_qn, d_ff_3_qn, d_ff_4_qn;

  D_Flip_Flop d_ff_1 (.D(d_ff_1_qn), .clk(clk), .Q(Up[0]), .Qn(d_ff_1_qn), .preset(rst));  // open: reset
  D_Flip_Flop d_ff_2 (.D(d_ff_2_qn), .clk(Up[0]), .Q(Up[1]), .Qn(d_ff_2_qn), .preset(rst));  // open: reset
  D_Flip_Flop d_ff_3 (.D(d_ff_3_qn), .clk(Up[1]), .Q(Up[2]), .Qn(d_ff_3_qn), .preset(rst));  // open: reset
  D_Flip_Flop d_ff_4 (.D(d_ff_4_qn), .clk(Up[2]), .Q(Up[3]), .Qn(d_ff_4_qn), .preset(rst));  // open: reset
endmodule

module Asynchronous_Decade_Counter (
  input  clk,
  input  Reset,
  output [3:0] Decade
);

  wire and_1_out, d_ff_1_qn, d_ff_2_qn, d_ff_3_qn, d_ff_4_qn, or_1_out;

  D_Flip_Flop d_ff_1 (.D(d_ff_1_qn), .clk(clk), .Q(Decade[0]), .Qn(d_ff_1_qn), .reset(or_1_out));  // open: preset
  or or_1 (or_1_out, Reset, and_1_out);
  D_Flip_Flop d_ff_2 (.D(d_ff_2_qn), .clk(d_ff_1_qn), .Q(Decade[1]), .Qn(d_ff_2_qn), .reset(or_1_out));  // open: preset
  D_Flip_Flop d_ff_3 (.D(d_ff_3_qn), .clk(d_ff_2_qn), .Q(Decade[2]), .Qn(d_ff_3_qn), .reset(or_1_out));  // open: preset
  D_Flip_Flop d_ff_4 (.D(d_ff_4_qn), .clk(d_ff_3_qn), .Q(Decade[3]), .Qn(d_ff_4_qn), .reset(or_1_out));  // open: preset
  and and_1 (and_1_out, Decade[3], Decade[1]);
endmodule

module Synchronous_Ring_Counter (
  input  clk,
  input  Reset,
  output [3:0] Ring
);

  D_Flip_Flop d_ff_1 (.D(Ring[3]), .clk(clk), .Q(Ring[0]), .preset(Reset));  // open: Qn, reset
  D_Flip_Flop d_ff_2 (.D(Ring[0]), .clk(clk), .Q(Ring[1]), .reset(Reset));  // open: Qn, preset
  D_Flip_Flop d_ff_3 (.D(Ring[1]), .clk(clk), .Q(Ring[2]), .reset(Reset));  // open: Qn, preset
  D_Flip_Flop d_ff_4 (.D(Ring[2]), .clk(clk), .Q(Ring[3]), .reset(Reset));  // open: Qn, preset
endmodule

module Synchronous_Johnson_Counter (
  input  clk,
  input  Reset,
  output [3:0] Johnson
);

  wire d_ff_4_qn;

  D_Flip_Flop d_ff_1 (.D(d_ff_4_qn), .clk(clk), .Q(Johnson[0]), .preset(Reset));  // open: Qn, reset
  D_Flip_Flop d_ff_2 (.D(Johnson[0]), .clk(clk), .Q(Johnson[1]), .reset(Reset));  // open: Qn, preset
  D_Flip_Flop d_ff_3 (.D(Johnson[1]), .clk(clk), .Q(Johnson[2]), .reset(Reset));  // open: Qn, preset
  D_Flip_Flop d_ff_4 (.D(Johnson[2]), .clk(clk), .Q(Johnson[3]), .Qn(d_ff_4_qn), .reset(Reset));  // open: preset
endmodule

module Universal (
  input  clk,
  input  rst,
  input  [2:0] in_3,
  output [3:0] out_4
);

  wire [3:0] asynchronous_decade_counter_1_decade, asynchronous_down_counter_1_up,
       asynchronous_up_counter_1_up, synchronous_johnson_counter_1_johnson, synchronous_ring_counter_1_ring;

  Asynchronous_Up_Counter asynchronous_up_counter_1 (.clk(clk), .rst(rst), .Up(asynchronous_up_counter_1_up));
  Asynchronous_Down_Counter asynchronous_down_counter_1 (.clk(clk), .rst(rst), .Up(asynchronous_down_counter_1_up));
  Asynchronous_Decade_Counter asynchronous_decade_counter_1 (
    .clk(clk), .Reset(rst), .Decade(asynchronous_decade_counter_1_decade));
  Synchronous_Ring_Counter synchronous_ring_counter_1 (.clk(clk), .Reset(rst), .Ring(synchronous_ring_counter_1_ring));
  Synchronous_Johnson_Counter synchronous_johnson_counter_1 (
    .clk(clk), .Reset(rst), .Johnson(synchronous_johnson_counter_1_johnson));
  Multiplexer #(.select(3), .width(4)) multiplexer_1 (
    .in0(asynchronous_up_counter_1_up), .in1(asynchronous_down_counter_1_up),
    .in2(asynchronous_decade_counter_1_decade), .in3(synchronous_ring_counter_1_ring),
    .in4(synchronous_johnson_counter_1_johnson), .out(out_4), .sel(in_3));  // open: in5, in6, in7
endmodule

module Main_Circuit_Up (
  input  Reset
);

  wire clk_out;
  wire [3:0] asynchronous_up_counter_1_up;

  Clock #(.highDuration(4), .lowDuration(4)) clk (.out(clk_out));
  Clock sysclk ();  // open: out
  // Probe on asynchronous_up_counter_1_up
  Asynchronous_Up_Counter asynchronous_up_counter_1 (.clk(clk_out), .rst(Reset), .Up(asynchronous_up_counter_1_up));
  Hex_Digit_Display hex_digit_display_1 (.value(asynchronous_up_counter_1_up));  // open: dp
endmodule
